// Logisim project A1-HeloisaV.circ as structural Verilog: 6 circuits, main circuit main
module main (
  input  in_1,
  input  in_2,
  output [7:0] out_3
);

  wire and_1_out, Branch, button_1_out, button_2_out, Clk, DataJump, Jump, M_R, M_W, MemToReg, not_1_out,
       or_1_out, R1_W_Adress, ula_1_out_somador, ula_1_out_subtrator, ula_1_zero, ULA_src, W_E;
  wire [1:0] multiplexer_2_out;
  wire [3:0] rom_1_data, rom_1_data_2, ULA_op;
  wire [7:0] adder_1_out, adder_2_out, bancoregistradores_1_datareg2, Data1, Immediate, multiplexer_1_out,
       multiplexer_4_out, PC, ram_1_dout, register_1_q, ula_1_ula_result;

  Clock clock_1 (.out(Clk));
  Register register_1 (.D(PC), .en(not_1_out), .clk(Clk), .Q(register_1_q), .clr(button_1_out));
  not not_1 (not_1_out, Clk);
  Button button_1 (.out(button_1_out));
  // Probe on register_1_q
  ROM rom_1 (.addr(register_1_q), .data({rom_1_data_2, rom_1_data}));
  Adder adder_1 (.a(register_1_q), .b(Immediate), .out(adder_1_out), .cin(1'b0), .cout(in_2));
  // Probe on rom_1_data_2
  // Probe on adder_1_out
  // Probe on out_3
  Multiplexer #(.width(8)) multiplexer_1 (
    .in0(adder_1_out), .in1(bancoregistradores_1_datareg2), .out(multiplexer_1_out), .sel(DataJump));
  Multiplexer #(.width(2)) multiplexer_2 (
    .in0(2'b00), .in1(rom_1_data[3:2]), .out(multiplexer_2_out), .sel(R1_W_Adress));
  Adder adder_2 (.a(8'h1), .b(register_1_q), .out(adder_2_out), .cin(1'b0), .cout(in_1));
  // Probe on bancoregistradores_1_datareg2
  // Probe on multiplexer_2_out
  Button button_2 (.out(button_2_out));
  // Probe on rom_1_data[1:0]
  assign Immediate = {{4{1'b0}}, rom_1_data};  // Bit_Extender bit_extender_1
  Control control_1 (
    .opcode(rom_1_data_2), .r1_w_addres(R1_W_Adress), .W_enable(W_E), .ULA_src(ULA_src), .ULA_op(ULA_op),
    .mem_read(M_R), .Mem_write(M_W), .MemToReg(MemToReg), .DataJump(DataJump), .Branch(Branch), .Jump(Jump));
  Multiplexer #(.width(8)) multiplexer_3 (.in0(adder_2_out), .in1(multiplexer_1_out), .out(PC), .sel(or_1_out));
  or or_1 (or_1_out, and_1_out, Jump);
  BancoRegistradores bancoregistradores_1 (
    .DataIn(out_3), .AddressReg1(multiplexer_2_out), .AddressReg2(rom_1_data[1:0]), .WriteEnable(W_E),
    .WriteAddress(multiplexer_2_out), .Clk(Clk), .Reset(button_2_out), .DataReg1(Data1),
    .DataReg2(bancoregistradores_1_datareg2));
  // Probe on Immediate
  // Probe on Data1
  Multiplexer #(.width(8)) multiplexer_4 (
    .in0(bancoregistradores_1_datareg2), .in1(Immediate), .out(multiplexer_4_out), .sel(ULA_src));
  and and_1 (and_1_out, ula_1_zero, Branch);
  // Probe on ULA_op
  LED out_sub (.in(ula_1_out_subtrator));
  LED out_soma (.in(ula_1_out_somador));
  ULA ula_1 (
    .Data1(Data1), .Data2(multiplexer_4_out), .ULA_Control(ULA_op), .Zero(ula_1_zero),
    .out_somador(ula_1_out_somador), .ULA_Result(ula_1_ula_result), .out_subtrator(ula_1_out_subtrator));
  // Probe on Data1
  // Probe on ula_1_ula_result
  RAM ram_1 (.addr(ula_1_ula_result), .we(M_W), .oe(M_R), .clk(Clk), .din(Data1), .dout(ram_1_dout));
  // Probe on ram_1_dout
  Multiplexer #(.width(8)) multiplexer_5 (.in0(ula_1_ula_result), .in1(ram_1_dout), .out(out_3), .sel(MemToReg));

  // Other names for the same wires on the sheet: WData[7:0] = out_3

  // Notes on the sheet:
  //   contents of rom_1 (hex, n*v repeats v):
  //   80 64 70 8a 69 6d 91 4b 4c 9b 70 6d 8a 9c 9c 5b a1 68 70 81 a8 62 70 15 81 94 82 20 80 70 64 68 6c
endmodule

module BancoRegistradores (
  input  [7:0] DataIn,
  input  [1:0] AddressReg1,
  input  [1:0] AddressReg2,
  input  WriteEnable,
  input  [1:0] WriteAddress,
  input  Clk,
  input  Reset,
  output [7:0] DataReg1,
  output [7:0] DataReg2
);

  wire demultiplexer_1_out0, demultiplexer_1_out1, demultiplexer_1_out2, demultiplexer_1_out3;
  wire [7:0] R0_q, R1_q, R2_q, R3_q;

  Demultiplexer #(.select(2)) demultiplexer_1 (
    .out0(demultiplexer_1_out0), .out1(demultiplexer_1_out1), .out2(demultiplexer_1_out2),
    .out3(demultiplexer_1_out3), .in(WriteEnable), .sel(WriteAddress));
  Register R0 (.D(DataIn), .en(demultiplexer_1_out0), .clk(Clk), .Q(R0_q), .clr(Reset));
  Register R1 (.D(DataIn), .en(demultiplexer_1_out1), .clk(Clk), .Q(R1_q), .clr(Reset));
  Register R2 (.D(DataIn), .en(demultiplexer_1_out2), .clk(Clk), .Q(R2_q), .clr(Reset));
  Register R3 (.D(DataIn), .en(demultiplexer_1_out3), .clk(Clk), .Q(R3_q), .clr(Reset));
  Multiplexer #(.select(2), .width(8)) multiplexer_1 (
    .in0(R0_q), .in1(R1_q), .in2(R2_q), .in3(R3_q), .out(DataReg1), .sel(AddressReg1));
  Multiplexer #(.select(2), .width(8)) multiplexer_2 (
    .in0(R0_q), .in1(R1_q), .in2(R2_q), .in3(R3_q), .out(DataReg2), .sel(AddressReg2));

  // Other names for the same wires on the sheet: AddReg1[1:0] = AddressReg1; AddReg2[1:0] = AddressReg2
endmodule

module Moves (
  input  [7:0] R0,
  input  [7:0] Imm,
  output [7:0] Move_High,
  output [7:0] Move_Low
);

  BitSelector #(.group(4)) bitselector_1 (.in(Imm), .out(Move_High[7:4]), .sel(1'b0));

  assign Move_High[3:0] = R0[3:0];
  assign Move_Low = {R0[7:4], Move_High[7:4]};
endmodule

module Shift (
  input  [7:0] Rb,
  input  [7:0] Ra,
  output [7:0] Shift_Left,
  output [7:0] Shift_Right
);

  wire or_1_out, or_2_out;
  wire [7:0] shifter_1_out, shifter_2_out;

  Shifter shifter_1 (.in(Ra), .\dist (Rb[2:0]), .out(shifter_1_out));
  Shifter #(.shift("lr")) shifter_2 (.in(Ra), .\dist (Rb[2:0]), .out(shifter_2_out));
  Multiplexer #(.width(8)) multiplexer_1 (.in0(shifter_1_out), .in1({8{1'b0}}), .out(Shift_Left), .sel(or_1_out));
  or or_1 (or_1_out, Rb[3], Rb[4], Rb[5], Rb[6], Rb[7]);
  Multiplexer #(.width(8)) multiplexer_2 (.in0(shifter_2_out), .in1({8{1'b0}}), .out(Shift_Right), .sel(or_2_out));
  or or_2 (or_2_out, Rb[3], Rb[4], Rb[5], Rb[6], Rb[7]);
endmodule

module ULA (
  input  [7:0] Data1,
  input  [7:0] Data2,
  input  [3:0] ULA_Control,
  output Zero,
  output out_somador,
  output [7:0] ULA_Result,
  output out_subtrator
);

  wire [7:0] adder_1_out, and_1_out, moves_1_move_high, moves_1_move_low, not_1_out, or_1_out,
       shift_1_shift_left, shift_1_shift_right, subtractor_1_out;

  Adder adder_1 (.a(Data1), .b(Data2), .out(adder_1_out), .cin(1'b0), .cout(out_somador));
  Subtractor subtractor_1 (.a(Data1), .b(Data2), .out(subtractor_1_out), .bin(1'b0), .bout(out_subtrator));
  assign and_1_out = Data1 & Data2;  // AND_Gate and_1, 8 bits wide
  assign or_1_out = Data1 | Data2;  // OR_Gate or_1, 8 bits wide
  assign not_1_out = ~Data2;  // NOT_Gate not_1, 8 bits wide
  Shift shift_1 (.Rb(Data2), .Ra(Data1), .Shift_Left(shift_1_shift_left), .Shift_Right(shift_1_shift_right));
  Moves moves_1 (.R0(Data1), .Imm(Data2), .Move_High(moves_1_move_high), .Move_Low(moves_1_move_low));
  Multiplexer #(.select(4), .width(8)) multiplexer_1 (
    .in0({8{1'b0}}), .in1(Data1), .in2(Data2), .in3(adder_1_out), .in4(subtractor_1_out), .in5(and_1_out),
    .in6(or_1_out), .in7(not_1_out), .in8(shift_1_shift_left), .in9(shift_1_shift_right),
    .in10(moves_1_move_high), .in11(moves_1_move_low), .in12({8{1'b0}}), .in13({8{1'b0}}), .in14({8{1'b0}}),
    .in15({8{1'b0}}), .out(ULA_Result), .sel(ULA_Control));
  nor nor_1 (Zero, ULA_Result[0], ULA_Result[1], ULA_Result[2], ULA_Result[3], ULA_Result[4], ULA_Result[5], ULA_Result[6], ULA_Result[7]);
endmodule

module Control (
  input  [3:0] opcode,
  output r1_w_addres,
  output W_enable,
  output ULA_src,
  output [3:0] ULA_op,
  output mem_read,
  output Mem_write,
  output MemToReg,
  output DataJump,
  output Branch,
  output Jump
);

  wire and_1_out, and_2_out, and_3_out, and_4_out, and_5_out, and_6_out, and_7_out, and_8_out, and_9_out,
       and_10_out, and_11_out, and_12_out, and_13_out, and_14_out, and_15_out, and_16_out, and_17_out,
       not_1_out, not_2_out, not_3_out;

  not not_1 (not_1_out, opcode[3]);
  not not_2 (not_2_out, opcode[2]);
  not not_3 (not_3_out, opcode[1]);
  not not_4 (DataJump, opcode[0]);
  and and_1 (and_1_out, not_1_out, DataJump);
  and and_2 (and_2_out, opcode[2], not_3_out);
  and and_3 (and_3_out, opcode[3], opcode[0]);
  and and_4 (and_4_out, opcode[1], DataJump);
  and and_5 (and_5_out, opcode[2], DataJump);
  and and_6 (and_6_out, opcode[2], opcode[1]);
  and and_7 (and_7_out, not_1_out, opcode[1], opcode[0]);
  and and_8 (and_8_out, not_2_out, not_3_out, DataJump);
  and and_9 (and_9_out, opcode[3], not_2_out, not_3_out, DataJump);
  and and_10 (and_10_out, opcode[3], opcode[2], opcode[1]);
  and and_11 (and_11_out, not_1_out, opcode[1], opcode[0]);
  and and_12 (and_12_out, not_2_out, opcode[1]);
  and and_13 (and_13_out, opcode[3], opcode[2], not_3_out);
  and and_14 (and_14_out, opcode[3], not_3_out);
  and and_15 (and_15_out, not_1_out, opcode[2]);
  and and_16 (and_16_out, not_2_out, not_3_out);
  and and_17 (and_17_out, opcode[3], opcode[0]);
  and and_18 (mem_read, not_1_out, opcode[2], not_3_out, DataJump);
  and and_19 (Mem_write, not_1_out, opcode[2], not_3_out, opcode[0]);
  and and_20 (MemToReg, not_1_out, opcode[2], not_3_out, DataJump);
  and and_21 (Branch, not_1_out, not_2_out, not_3_out);
  and and_22 (Jump, not_1_out, not_2_out, opcode[1]);
  or or_1 (r1_w_addres, and_1_out, and_2_out, and_3_out, and_4_out);
  or or_2 (W_enable, and_5_out, and_6_out, opcode[3]);
  or or_3 (ULA_src, and_7_out, and_8_out);
  or or_4 (ULA_op[3], and_9_out, and_10_out, and_11_out);
  or or_5 (ULA_op[2], and_12_out, and_13_out);
  or or_6 (ULA_op[1], and_14_out, and_15_out);
  or or_7 (ULA_op[0], and_16_out, and_17_out);
endmodule
