// Logisim project Trab2 - HeloisaV.circ as structural Verilog: 10 circuits, main circuit main
module main (
  input  in_1
);

  wire and_1_out, Branch, Clk, M_R, M_W, MemToReg, MEMtoREGv, MRv, MWv, not_1_out, R1_W_Adress, R1Wsrcv,
       Reset, ULA_src, ulaescalar_1_zero, ULAsrcv, W_E, WEv;
  wire [1:0] multiplexer_1_out, multiplexer_2_out, multiplexer_3_out, multiplexer_4_out, multiplexer_5_out,
       rom_1_data, rom_1_data_2;
  wire [2:0] ULA_op, ULAopv;
  wire [3:0] rom_1_data_3;
  wire [7:0] adder_1_out, bancoregistradores0_1_datareg2, bancoregistradores0_2_datareg2,
       bancoregistradores1_1_datareg2, bancoregistradores2_1_datareg2, bancoregistradores3_1_datareg2,
       bit_extender_2_out, Data1, Data1v0, Data1v1, Data1v2, Data1v3, IMMv, multiplexer_6_out,
       multiplexer_7_out, multiplexer_8_out, multiplexer_9_out, multiplexer_10_out, multiplexer_11_out,
       multiplexer_12_out, multiplexer_13_out, multiplexer_14_out, multiplexer_15_out, multiplexer_16_out,
       multiplexer_17_out, ram_1_dout, ram_2_dout, ram_3_dout, ram_4_dout, ram_5_dout, register_1_q,
       ulaescalar_1_ula_result, ulavetorial_1_ula_result, ulavetorial_2_ula_result, ulavetorial_3_ula_result,
       ulavetorial_4_ula_result;

  Button button_1 (.out(Reset));
  Clock clock_1 (.out(Clk));
  Register register_1 (.D(multiplexer_8_out), .en(not_1_out), .clk(Clk), .Q(register_1_q), .clr(Reset));
  not not_1 (not_1_out, Clk);
  // Probe on register_1_q
  ROM rom_1 (.addr(register_1_q), .data({rom_1_data_3, rom_1_data_2, rom_1_data}));
  // Probe on {rom_1_data_2, rom_1_data}
  // Probe on rom_1_data_3
  assign IMMv = {{4{1'b0}}, {rom_1_data_2, rom_1_data}};  // Bit_Extender bit_extender_1
  // Probe on rom_1_data_2
  // Probe on rom_1_data
  Multiplexer #(.width(2)) multiplexer_1 (.in0(rom_1_data_2), .in1(2'b01), .out(multiplexer_1_out), .sel(R1_W_Adress));
  assign bit_extender_2_out = {{4{1'b0}}, {rom_1_data_2, rom_1_data}};  // Bit_Extender bit_extender_2
  // Probe on rom_1_data_3
  // Probe on multiplexer_2_out
  Multiplexer #(.width(2)) multiplexer_2 (.in0(rom_1_data_2), .in1(2'b01), .out(multiplexer_2_out), .sel(R1Wsrcv));
  // Probe on rom_1_data
  Multiplexer #(.width(2)) multiplexer_3 (.in0(rom_1_data_2), .in1(2'b01), .out(multiplexer_3_out), .sel(R1Wsrcv));
  Multiplexer #(.width(2)) multiplexer_4 (.in0(rom_1_data_2), .in1(2'b01), .out(multiplexer_4_out), .sel(R1Wsrcv));
  Multiplexer #(.width(2)) multiplexer_5 (.in0(rom_1_data_2), .in1(2'b01), .out(multiplexer_5_out), .sel(R1Wsrcv));
  // Probe on multiplexer_13_out
  // Probe on multiplexer_1_out
  // Probe on multiplexer_15_out
  // Probe on multiplexer_16_out
  // Probe on multiplexer_17_out
  // Probe on rom_1_data
  // Probe on multiplexer_14_out
  Adder adder_1 (.a(8'h1), .b(register_1_q), .out(adder_1_out), .cin(1'b0), .cout(in_1));
  Multiplexer #(.width(8)) multiplexer_6 (
    .in0(bit_extender_2_out), .in1({8{1'b0}}), .out(multiplexer_6_out), .sel(Branch));
  ControleEscalar controleescalar_1 (
    .Opcode(rom_1_data_3), .R1_W_Adress(R1_W_Adress), .W_E(W_E), .ULA_src(ULA_src), .ULAop(ULA_op),
    .MEM_Read(M_R), .MEM_Write(M_W), .MemToReg(MemToReg), .Branch(Branch));
  BancoRegistradores0 bancoregistradores0_1 (
    .DataIn(multiplexer_13_out), .AddressReg1(multiplexer_1_out), .AddressReg2(rom_1_data),
    .WriteEnable(W_E), .WriteAddress(multiplexer_1_out), .Clk(Clk), .Reset(Reset), .DataReg1(Data1),
    .DataReg2(bancoregistradores0_1_datareg2));
  BancoRegistradores0 bancoregistradores0_2 (
    .DataIn(multiplexer_14_out), .AddressReg1(multiplexer_2_out), .AddressReg2(rom_1_data),
    .WriteEnable(WEv), .WriteAddress(multiplexer_2_out), .Clk(Clk), .Reset(Reset), .DataReg1(Data1v0),
    .DataReg2(bancoregistradores0_2_datareg2));
  BancoRegistradores1 bancoregistradores1_1 (
    .DataIn(multiplexer_15_out), .AddressReg1(multiplexer_3_out), .AddressReg2(rom_1_data),
    .WriteEnable(WEv), .WriteAddress(multiplexer_3_out), .Clk(Clk), .Reset(Reset), .DataReg1(Data1v1),
    .DataReg2(bancoregistradores1_1_datareg2));
  BancoRegistradores2 bancoregistradores2_1 (
    .DataIn(multiplexer_16_out), .AddressReg1(multiplexer_4_out), .AddressReg2(rom_1_data),
    .WriteEnable(WEv), .WriteAddress(multiplexer_4_out), .Clk(Clk), .Reset(Reset), .DataReg1(Data1v2),
    .DataReg2(bancoregistradores2_1_datareg2));
  BancoRegistradores3 bancoregistradores3_1 (
    .DataIn(multiplexer_17_out), .AddressReg1(multiplexer_5_out), .AddressReg2(rom_1_data),
    .WriteEnable(WEv), .WriteAddress(multiplexer_5_out), .Clk(Clk), .Reset(Reset), .DataReg1(Data1v3),
    .DataReg2(bancoregistradores3_1_datareg2));
  // Probe on bancoregistradores0_1_datareg2
  Multiplexer #(.width(8)) multiplexer_7 (
    .in0(bancoregistradores0_1_datareg2), .in1(multiplexer_6_out), .out(multiplexer_7_out), .sel(ULA_src));
  // Probe on multiplexer_6_out
  Multiplexer #(.width(8)) multiplexer_8 (
    .in0(adder_1_out), .in1(bancoregistradores0_1_datareg2), .out(multiplexer_8_out), .sel(and_1_out));
  // Probe on ULA_op
  // Probe on Data1v0
  Multiplexer #(.width(8)) multiplexer_9 (
    .in0(bancoregistradores0_2_datareg2), .in1(IMMv), .out(multiplexer_9_out), .sel(ULAsrcv));
  // Probe on multiplexer_9_out
  Multiplexer #(.width(8)) multiplexer_10 (
    .in0(bancoregistradores1_1_datareg2), .in1(IMMv), .out(multiplexer_10_out), .sel(ULAsrcv));
  Multiplexer #(.width(8)) multiplexer_11 (
    .in0(bancoregistradores2_1_datareg2), .in1(IMMv), .out(multiplexer_11_out), .sel(ULAsrcv));
  // Probe on Data1v3
  Multiplexer #(.width(8)) multiplexer_12 (
    .in0(bancoregistradores3_1_datareg2), .in1(IMMv), .out(multiplexer_12_out), .sel(ULAsrcv));
  // Probe on multiplexer_12_out
  and and_1 (and_1_out, Branch, ulaescalar_1_zero);
  ULAescalar ulaescalar_1 (
    .Data1(Data1), .Data2(multiplexer_7_out), .ULA_Control(ULA_op), .Zero(ulaescalar_1_zero),
    .ULA_Result(ulaescalar_1_ula_result));
  // Probe on Data1
  ULAvetorial ulavetorial_1 (
    .Data1(Data1v0), .Data2(multiplexer_9_out), .ULAcontrol(ULAopv), .ULA_Result(ulavetorial_1_ula_result));
  ULAvetorial ulavetorial_2 (
    .Data1(Data1v1), .Data2(multiplexer_10_out), .ULAcontrol(ULAopv), .ULA_Result(ulavetorial_2_ula_result));
  ULAvetorial ulavetorial_3 (
    .Data1(Data1v2), .Data2(multiplexer_11_out), .ULAcontrol(ULAopv), .ULA_Result(ulavetorial_3_ula_result));
  ULAvetorial ulavetorial_4 (
    .Data1(Data1v3), .Data2(multiplexer_12_out), .ULAcontrol(ULAopv), .ULA_Result(ulavetorial_4_ula_result));
  // Probe on ulaescalar_1_ula_result
  RAM #(.asyncread("true")) ram_1 (
    .addr(ulaescalar_1_ula_result), .we(M_W), .oe(M_R), .clk(Clk), .din(Data1), .dout(ram_1_dout));
  ControleVetorial controlevetorial_1 (
    .Opcode(rom_1_data_3), .R1_W_Adressv(R1Wsrcv), .W_Ev(WEv), .ULA_srcv(ULAsrcv), .ULAopv(ULAopv),
    .MEM_Readv(MRv), .MEM_Writev(MWv), .MemToRegv(MEMtoREGv));
  RAM #(.asyncread("true")) ram_2 (
    .addr(ulavetorial_1_ula_result), .we(MWv), .oe(MRv), .clk(Clk), .din(Data1v0), .dout(ram_2_dout));
  RAM #(.asyncread("true")) ram_3 (
    .addr(ulavetorial_2_ula_result), .we(MWv), .oe(MRv), .clk(Clk), .din(Data1v1), .dout(ram_3_dout));
  RAM #(.asyncread("true")) ram_4 (
    .addr(ulavetorial_3_ula_result), .we(MWv), .oe(MRv), .clk(Clk), .din(Data1v2), .dout(ram_4_dout));
  RAM #(.asyncread("true")) ram_5 (
    .addr(ulavetorial_4_ula_result), .we(MWv), .oe(MRv), .clk(Clk), .din(Data1v3), .dout(ram_5_dout));
  // Probe on ram_1_dout
  // Probe on multiplexer_13_out
  Multiplexer #(.width(8)) multiplexer_13 (
    .in0(ulaescalar_1_ula_result), .in1(ram_1_dout), .out(multiplexer_13_out), .sel(MemToReg));
  Multiplexer #(.width(8)) multiplexer_14 (
    .in0(ulavetorial_1_ula_result), .in1(ram_2_dout), .out(multiplexer_14_out), .sel(MEMtoREGv));
  Multiplexer #(.width(8)) multiplexer_15 (
    .in0(ulavetorial_2_ula_result), .in1(ram_3_dout), .out(multiplexer_15_out), .sel(MEMtoREGv));
  Multiplexer #(.width(8)) multiplexer_16 (
    .in0(ulavetorial_3_ula_result), .in1(ram_4_dout), .out(multiplexer_16_out), .sel(MEMtoREGv));
  Multiplexer #(.width(8)) multiplexer_17 (
    .in0(ulavetorial_4_ula_result), .in1(ram_5_dout), .out(multiplexer_17_out), .sel(MEMtoREGv));
  // Probe on multiplexer_14_out
  // Probe on multiplexer_15_out
  // Probe on multiplexer_16_out
  // Probe on multiplexer_17_out

  // Notes on the sheet:
  //   contents of rom_1 (hex, n*v repeats v):
  //   a0 b4 cd c8 21 33 4d 20 33 49 7b 9a cb 20 31 59 20 3a 71 6c a0 b0 e9 ed 23 35 4d 20 33 49 7b a0 b0
  //   e9 a0 bc c9 a1 b4 c4 c7 c8 cb 96 a0 b4 cd 20 31 59 21 3e 71 6c a0 b0 e9 ed 25 32 4d 20 33 49 a0 b0
  //   c9 7b a1 b8 c7 c4 99 a0 b4 cd 20 31 59 24 33 71 6c ee 27 36 4d 20 33 49 7b a0 bc c8 c9 cb b0 c4 c7
  //   85 8a c9 a1 b8 c4 c7 99 a0 b4 cd b0 e9 20 31 59 25 3a 71
endmodule

module ControleEscalar (
  input  [3:0] Opcode,
  output R1_W_Adress,
  output W_E,
  output ULA_src,
  output [2:0] ULAop,
  output MEM_Read,
  output MEM_Write,
  output MemToReg,
  output Branch
);

  wire and_1_out, and_2_out, and_3_out, and_4_out, and_5_out, and_6_out, and_7_out, and_8_out, and_9_out,
       and_10_out, and_11_out, and_12_out, not_1_out, not_2_out, not_3_out, not_4_out;

  not not_1 (not_1_out, Opcode[3]);
  not not_2 (not_2_out, Opcode[2]);
  not not_3 (not_3_out, Opcode[1]);
  not not_4 (not_4_out, Opcode[0]);
  and and_1 (and_1_out, not_1_out, not_2_out, Opcode[1]);
  and and_2 (and_2_out, Opcode[3], not_3_out);
  and and_3 (and_3_out, Opcode[3], Opcode[2]);
  and and_4 (and_4_out, not_1_out, not_4_out);
  and and_5 (and_5_out, not_1_out, not_2_out, Opcode[1]);
  and and_6 (and_6_out, not_1_out, Opcode[2], not_3_out);
  and and_7 (and_7_out, not_2_out, Opcode[1]);
  and and_8 (and_8_out, not_1_out, Opcode[1], Opcode[0]);
  and and_9 (and_9_out, Opcode[2], Opcode[0]);
  and and_10 (and_10_out, not_3_out, not_4_out);
  and and_11 (and_11_out, not_2_out, Opcode[1], Opcode[0]);
  and and_12 (and_12_out, Opcode[2], not_4_out);
  and and_13 (MEM_Read, not_2_out, not_3_out, not_4_out);
  and and_14 (MEM_Write, not_1_out, not_2_out, not_3_out, Opcode[0]);
  and and_15 (MemToReg, not_2_out, not_3_out, not_4_out);
  and and_16 (Branch, not_1_out, Opcode[2], Opcode[1], Opcode[0]);
  or or_1 (R1_W_Adress, and_1_out, and_2_out, and_3_out);
  or or_2 (W_E, and_4_out, and_5_out, and_6_out);
  or or_3 (ULA_src, and_7_out, and_8_out);
  or or_4 (ULAop[2], Opcode[1], and_9_out);
  or or_5 (ULAop[1], not_2_out, and_10_out);
  or or_6 (ULAop[0], and_11_out, and_12_out);
endmodule

module ControleVetorial (
  input  [3:0] Opcode,
  output R1_W_Adressv,
  output W_Ev,
  output ULA_srcv,
  output [2:0] ULAopv,
  output MEM_Readv,
  output MEM_Writev,
  output MemToRegv
);

  wire and_2_out, and_3_out, and_4_out, and_6_out, and_7_out, and_8_out, not_1_out, not_2_out, not_3_out;

  not not_1 (not_1_out, Opcode[2]);
  not not_2 (not_2_out, Opcode[1]);
  not not_3 (not_3_out, Opcode[0]);
  and and_1 (R1_W_Adressv, not_1_out, Opcode[1]);
  and and_2 (and_2_out, Opcode[3], not_3_out);
  and and_3 (and_3_out, Opcode[3], Opcode[1]);
  and and_4 (and_4_out, Opcode[3], Opcode[2]);
  and and_5 (ULA_srcv, not_1_out, Opcode[1]);
  and and_6 (and_6_out, not_1_out, Opcode[1]);
  and and_7 (and_7_out, Opcode[2], not_2_out);
  and and_8 (and_8_out, not_1_out, not_2_out);
  and and_9 (MEM_Readv, not_1_out, not_2_out, not_3_out);
  and and_10 (MEM_Writev, Opcode[3], not_1_out, not_2_out, Opcode[0]);
  and and_11 (MemToRegv, Opcode[3], not_1_out, not_2_out, not_3_out);
  or or_1 (W_Ev, and_2_out, and_3_out, and_4_out);
  or or_2 (ULAopv[1], and_6_out, and_7_out);
  or or_3 (ULAopv[0], and_8_out, Opcode[0]);

  assign ULAopv[2] = Opcode[1];
endmodule

module BancoRegistradores0 (
  input  [7:0] DataIn,
  input  [1:0] AddressReg1,
  input  [1:0] AddressReg2,
  input  WriteEnable,
  input  [1:0] WriteAddress,
  input  Clk,
  input  Reset,
  output [7:0] DataReg1,
  output [7:0] DataReg2
);

  wire demultiplexer_1_out0, demultiplexer_1_out1, demultiplexer_1_out2, demultiplexer_1_out3;
  wire [7:0] R1_q, R2_q, R3_q;

  Demultiplexer #(.select(2)) demultiplexer_1 (
    .out0(demultiplexer_1_out0), .out1(demultiplexer_1_out1), .out2(demultiplexer_1_out2),
    .out3(demultiplexer_1_out3), .in(WriteEnable), .sel(WriteAddress));
  LED Wreg0 (.in(demultiplexer_1_out0));
  Register R1 (.D(DataIn), .en(demultiplexer_1_out1), .clk(Clk), .Q(R1_q), .clr(Reset));
  Register R2 (.D(DataIn), .en(demultiplexer_1_out2), .clk(Clk), .Q(R2_q), .clr(Reset));
  Register R3 (.D(DataIn), .en(demultiplexer_1_out3), .clk(Clk), .Q(R3_q), .clr(Reset));
  Multiplexer #(.select(2), .width(8)) multiplexer_1 (
    .in0({8{1'b0}}), .in1(R1_q), .in2(R2_q), .in3(R3_q), .out(DataReg1), .sel(AddressReg1));
  Multiplexer #(.select(2), .width(8)) multiplexer_2 (
    .in0({8{1'b0}}), .in1(R1_q), .in2(R2_q), .in3(R3_q), .out(DataReg2), .sel(AddressReg2));

  // Other names for the same wires on the sheet: AddReg1[1:0] = AddressReg1; AddReg2[1:0] = AddressReg2
endmodule

module BancoRegistradores1 (
  input  [7:0] DataIn,
  input  [1:0] AddressReg1,
  input  [1:0] AddressReg2,
  input  WriteEnable,
  input  [1:0] WriteAddress,
  input  Clk,
  input  Reset,
  output [7:0] DataReg1,
  output [7:0] DataReg2
);

  wire demultiplexer_1_out0, demultiplexer_1_out1, demultiplexer_1_out2, demultiplexer_1_out3;
  wire [7:0] R1_q, R2_q, R3_q;

  Demultiplexer #(.select(2)) demultiplexer_1 (
    .out0(demultiplexer_1_out0), .out1(demultiplexer_1_out1), .out2(demultiplexer_1_out2),
    .out3(demultiplexer_1_out3), .in(WriteEnable), .sel(WriteAddress));
  LED Wreg0 (.in(demultiplexer_1_out0));
  Register R1 (.D(DataIn), .en(demultiplexer_1_out1), .clk(Clk), .Q(R1_q), .clr(Reset));
  Register R2 (.D(DataIn), .en(demultiplexer_1_out2), .clk(Clk), .Q(R2_q), .clr(Reset));
  Register R3 (.D(DataIn), .en(demultiplexer_1_out3), .clk(Clk), .Q(R3_q), .clr(Reset));
  Multiplexer #(.select(2), .width(8)) multiplexer_1 (
    .in0(8'h1), .in1(R1_q), .in2(R2_q), .in3(R3_q), .out(DataReg1), .sel(AddressReg1));
  Multiplexer #(.select(2), .width(8)) multiplexer_2 (
    .in0(8'h1), .in1(R1_q), .in2(R2_q), .in3(R3_q), .out(DataReg2), .sel(AddressReg2));

  // Other names for the same wires on the sheet: AddReg1[1:0] = AddressReg1; AddReg2[1:0] = AddressReg2
endmodule

module BancoRegistradores2 (
  input  [7:0] DataIn,
  input  [1:0] AddressReg1,
  input  [1:0] AddressReg2,
  input  WriteEnable,
  input  [1:0] WriteAddress,
  input  Clk,
  input  Reset,
  output [7:0] DataReg1,
  output [7:0] DataReg2
);

  wire demultiplexer_1_out0, demultiplexer_1_out1, demultiplexer_1_out2, demultiplexer_1_out3;
  wire [7:0] R1_q, R2_q, R3_q;

  Demultiplexer #(.select(2)) demultiplexer_1 (
    .out0(demultiplexer_1_out0), .out1(demultiplexer_1_out1), .out2(demultiplexer_1_out2),
    .out3(demultiplexer_1_out3), .in(WriteEnable), .sel(WriteAddress));
  LED Wreg0 (.in(demultiplexer_1_out0));
  Register R1 (.D(DataIn), .en(demultiplexer_1_out1), .clk(Clk), .Q(R1_q), .clr(Reset));
  Register R2 (.D(DataIn), .en(demultiplexer_1_out2), .clk(Clk), .Q(R2_q), .clr(Reset));
  Register R3 (.D(DataIn), .en(demultiplexer_1_out3), .clk(Clk), .Q(R3_q), .clr(Reset));
  Multiplexer #(.select(2), .width(8)) multiplexer_1 (
    .in0(8'h2), .in1(R1_q), .in2(R2_q), .in3(R3_q), .out(DataReg1), .sel(AddressReg1));
  Multiplexer #(.select(2), .width(8)) multiplexer_2 (
    .in0(8'h2), .in1(R1_q), .in2(R2_q), .in3(R3_q), .out(DataReg2), .sel(AddressReg2));

  // Other names for the same wires on the sheet: AddReg1[1:0] = AddressReg1; AddReg2[1:0] = AddressReg2
endmodule

module BancoRegistradores3 (
  input  [7:0] DataIn,
  input  [1:0] AddressReg1,
  input  [1:0] AddressReg2,
  input  WriteEnable,
  input  [1:0] WriteAddress,
  input  Clk,
  input  Reset,
  output [7:0] DataReg1,
  output [7:0] DataReg2
);

  wire demultiplexer_1_out0, demultiplexer_1_out1, demultiplexer_1_out2, demultiplexer_1_out3;
  wire [7:0] R1_q, R2_q, R3_q;

  Demultiplexer #(.select(2)) demultiplexer_1 (
    .out0(demultiplexer_1_out0), .out1(demultiplexer_1_out1), .out2(demultiplexer_1_out2),
    .out3(demultiplexer_1_out3), .in(WriteEnable), .sel(WriteAddress));
  LED Wreg0 (.in(demultiplexer_1_out0));
  Register R1 (.D(DataIn), .en(demultiplexer_1_out1), .clk(Clk), .Q(R1_q), .clr(Reset));
  Register R2 (.D(DataIn), .en(demultiplexer_1_out2), .clk(Clk), .Q(R2_q), .clr(Reset));
  Register R3 (.D(DataIn), .en(demultiplexer_1_out3), .clk(Clk), .Q(R3_q), .clr(Reset));
  Multiplexer #(.select(2), .width(8)) multiplexer_1 (
    .in0(8'h3), .in1(R1_q), .in2(R2_q), .in3(R3_q), .out(DataReg1), .sel(AddressReg1));
  Multiplexer #(.select(2), .width(8)) multiplexer_2 (
    .in0(8'h3), .in1(R1_q), .in2(R2_q), .in3(R3_q), .out(DataReg2), .sel(AddressReg2));

  // Other names for the same wires on the sheet: AddReg1[1:0] = AddressReg1; AddReg2[1:0] = AddressReg2
endmodule

module ULAvetorial (
  input  [7:0] Data1,
  input  [7:0] Data2,
  input  [2:0] ULAcontrol,
  output [7:0] ULA_Result
);

  wire adder_1_cout, subtractor_1_bout;
  wire [7:0] adder_1_out, and_1_out, moves_1_move_high, moves_1_move_low, or_1_out, subtractor_1_out;

  Adder adder_1 (.a(Data1), .b(Data2), .out(adder_1_out), .cin(1'b0), .cout(adder_1_cout));
  LED led_1 (.in(adder_1_cout));
  Subtractor subtractor_1 (.a(Data1), .b(Data2), .out(subtractor_1_out), .bin(1'b0), .bout(subtractor_1_bout));
  LED led_2 (.in(subtractor_1_bout));
  assign and_1_out = Data1 & Data2;  // AND_Gate and_1, 8 bits wide
  assign or_1_out = Data1 | Data2;  // OR_Gate or_1, 8 bits wide
  Moves moves_1 (.R0(Data1), .Imm(Data2), .Move_High(moves_1_move_high), .Move_Low(moves_1_move_low));
  Multiplexer #(.select(3), .width(8)) multiplexer_1 (
    .in0(Data1), .in1(Data2), .in2(adder_1_out), .in3(subtractor_1_out), .in4(and_1_out), .in5(or_1_out),
    .in6(moves_1_move_high), .in7(moves_1_move_low), .out(ULA_Result), .sel(ULAcontrol));
endmodule

module ULAescalar (
  input  [7:0] Data1,
  input  [7:0] Data2,
  input  [2:0] ULA_Control,
  output Zero,
  output [7:0] ULA_Result
);

  wire adder_1_cout, subtractor_1_bout;
  wire [7:0] adder_1_out, and_1_out, moves_1_move_high, moves_1_move_low, subtractor_1_out;

  Adder adder_1 (.a(Data1), .b(Data2), .out(adder_1_out), .cin(1'b0), .cout(adder_1_cout));
  LED led_1 (.in(adder_1_cout));
  Subtractor subtractor_1 (.a(Data1), .b(Data2), .out(subtractor_1_out), .bin(1'b0), .bout(subtractor_1_bout));
  LED led_2 (.in(subtractor_1_bout));
  assign and_1_out = Data1 & Data2;  // AND_Gate and_1, 8 bits wide
  Moves moves_1 (.R0(Data1), .Imm(Data2), .Move_High(moves_1_move_high), .Move_Low(moves_1_move_low));
  Multiplexer #(.select(3), .width(8)) multiplexer_1 (
    .in0({8{1'b0}}), .in1(Data1), .in2(Data2), .in3(adder_1_out), .in4(subtractor_1_out), .in5(and_1_out),
    .in6(moves_1_move_high), .in7(moves_1_move_low), .out(ULA_Result), .sel(ULA_Control));
  nor nor_1 (Zero, ULA_Result[0], ULA_Result[1], ULA_Result[2], ULA_Result[3], ULA_Result[4], ULA_Result[5], ULA_Result[6], ULA_Result[7]);
endmodule

module Moves (
  input  [7:0] R0,
  input  [7:0] Imm,
  output [7:0] Move_High,
  output [7:0] Move_Low
);

  BitSelector #(.group(4)) bitselector_1 (.in(Imm), .out(Move_High[7:4]), .sel(1'b0));

  assign Move_High[3:0] = R0[3:0];
  assign Move_Low = {R0[7:4], Move_High[7:4]};
endmodule
